# Fritzing sketch strix-takeover-breadboard (saved by Fritzing 1.0.3)
breadboards: 1

parts:
  Nano1 = Arduino Nano (Rev3.0)
  R1 = Resistor [resistance=4.7kΩ package=THT]
  C1 = Ceramic Capacitor [capacitance=1µF package="100 mil [THT, multilayer]"]
  R2 = Resistor [resistance=4.7kΩ package=THT]
  C2 = Ceramic Capacitor [capacitance=1µF package="100 mil [THT, multilayer]"]
  SR04_frontRight = HC-SR04 Ultrasonic Distance Sensor
  SR04_frontLeft = HC-SR04 Ultrasonic Distance Sensor
  LevelShifter1 = I2C level shifter bidirectional
  ToF_VL53L4CD = Header 4 [package=jst-4-pth]

nets:
  GND: Nano1.GND, C1.1, C2.1, SR04_frontRight.GND, SR04_frontLeft.GND, LevelShifter1.GND, ToF_VL53L4CD.4
  N1: Nano1.D2, SR04_frontLeft.TRIG
  N2: Nano1.D3, SR04_frontLeft.ECHO
  N3: Nano1.D4, SR04_frontRight.TRIG
  N4: Nano1.D5, SR04_frontRight.ECHO
  N5: Nano1.D9, R1.Pin_0
  N6: Nano1.D10, R2.Pin_0
  VCC: Nano1.5V, SR04_frontRight.VCC, SR04_frontLeft.VCC, LevelShifter1.HV
  N7: Nano1.A5, LevelShifter1.HV2
  N8: Nano1.A4, LevelShifter1.HV1
  N9: Nano1.3V3, LevelShifter1.LV, ToF_VL53L4CD.3
  N10: R1.Pin_1, C1.0
  N11: R2.Pin_1, C2.0
  N12: LevelShifter1.LV2, ToF_VL53L4CD.2
  N13: LevelShifter1.LV1, ToF_VL53L4CD.1

notes:
  STRIX - controller takeover, Variant B (PWM wiper synthesis)
  The Nano synthesizes the two wiper voltages that the handheld
  controller's trigger and steering pots used to produce. Each
  channel is a 4.7k + 1uF RC low-pass filter on a Timer1 PWM pin.
  D9 = throttle, D10 = steering, A0 = controller rail sense.
  The Nano is rotated so its USB end faces the left board edge;
  the phone's OTG cable exits left and powers the Nano.
  FORWARD-PERCEPTION ARRAY (above the board)
  HC-SR04 ultrasonics, front-left and front-right corners:
  front-left TRIG/ECHO -> D2 / D3
  front-right TRIG/ECHO -> D4 / D5
  VCC -> top + rail, GND -> top - rail
  Mount them on the corners angled ~15 deg outward at bumper
  height. Left/right is the CAR's perspective, not yours.
  Placement and aiming: docs/sensor-wiring.md
  3.3V TIME-OF-FLIGHT SENSOR - the centre beam
  The 4-pin header stands in for the VL53L4CD / Modulino
  Distance module; Fritzing has no part for it.
  SDA/SCL cross a bidirectional I2C level shifter: the Nano's
  I2C is 5V logic and the module is 3.3V-only and NOT 5V
  tolerant. HV side faces the Nano (A4/A5 + 5V), LV side faces
  the module.
  ORANGE 3V3 runs straight off the Nano's 3V3 pin - never a 5V
  rail - and drives only this module (~50mA budget).
  TO THE HANDHELD CONTROLLER (loose ends, below)
  BLUE -> TRIGGER pot WIPER pin
  GREEN -> WHEEL pot WIPER pin
  PURPLE -> pot HIGH / rail pin, into A0
  BLACK -> controller GROUND (pot LOW pin)
  PURPLE is the rail sense: it scales every PWM duty to the
  sagging AA rail so calibrated neutral cannot drift. Do not
  omit it.
  Identify which harness wire is the wiper BEFORE cutting - see
  docs/pot-identification.md. On this build's Hosim controller
  the BLACK harness wire was the wiper.
